# Fritzing sketch main (saved by Fritzing 0.9.6b)
breadboards: 1

parts:
  PIC_16F877A1 = PIC 16F877A [package=THT]
  U1 = 7-SEGMENT-DISPLAY [package=7-segment-display]
  R1 = Resistor [tolerance=±5% power=0.25 resistance=220 package=THT]
  R2 = Resistor [tolerance=±5% power=0.25 resistance=220 package=THT]
  R3 = Resistor [tolerance=±5% power=0.25 resistance=220 package=THT]
  R4 = Resistor [tolerance=±5% power=0.25 resistance=220 package=THT]
  R5 = Resistor [tolerance=±5% power=0.25 resistance=220 package=THT]
  R6 = Resistor [tolerance=±5% power=0.25 resistance=220 package=THT]
  R7 = Resistor [tolerance=±5% power=0.25 resistance=220 package=THT]
  LED1 = LED - 5mm [color="Red (633nm)" current=0.030 package="5 mm [THT]"]
  R8 = Resistor [tolerance=±5% power=0.25 resistance=220 package=THT]
  SW1 = DIP Switch 8 Position [package=dipswitch-08]
  R9 = Resistor [tolerance=±5% power=0.25 resistance=1k package=THT]
  R10 = Resistor [tolerance=±5% power=0.25 resistance=1k package=THT]
  R11 = Resistor [tolerance=±5% power=0.25 resistance=1k package=THT]
  R12 = Resistor [tolerance=±5% power=0.25 resistance=1k package=THT]
  R13 = Resistor [tolerance=±5% power=0.25 resistance=1k package=THT]

nets:
  N1: PIC_16F877A1.RA0/AN0, SW1.2, R10.Pin_0
  N2: PIC_16F877A1.RA1/AN1, SW1.1, R9.Pin_0
  N3: PIC_16F877A1.RA2/AN2, SW1.4, R12.Pin_0
  N4: PIC_16F877A1.RA3/AN3, SW1.3, R11.Pin_0
  N5: PIC_16F877A1.RA4, SW1.5, R13.Pin_0
  N6: PIC_16F877A1.VSS#30, U1.C, R8.Pin_1, R9.Pin_1, R10.Pin_1, R11.Pin_1, R12.Pin_1, R13.Pin_1
  N7: PIC_16F877A1.VDD#31, SW1.12, SW1.13, SW1.14, SW1.15, SW1.16
  N8: PIC_16F877A1.RB0/INT, LED1.anode
  N9: PIC_16F877A1.RB1, R7.Pin_0
  N10: PIC_16F877A1.RB2, R6.Pin_0
  N11: PIC_16F877A1.RB3, R5.Pin_0
  N12: PIC_16F877A1.RB4, R4.Pin_0
  N13: PIC_16F877A1.RB5, R3.Pin_0
  N14: PIC_16F877A1.RB6, R2.Pin_0
  N15: PIC_16F877A1.RB7, R1.Pin_0
  N16: U1.E, R7.Pin_1
  N17: U1.D, R5.Pin_1
  N18: U1.G1, R4.Pin_1
  N19: U1.DP, R3.Pin_1
  N20: U1.A, R2.Pin_1
  N21: U1.G2, R1.Pin_1
  N22: U1.G, R6.Pin_1
  N23: LED1.cathode, R8.Pin_0
